# Fritzing sketch Prototyp_v1 (saved by Fritzing 0.9.3b)
breadboards: 1

parts:
  MOD-WIFI-ESP8266-DEV1 = Olimex ESP8266 DEV
  PIR1 = PIR sensor
  PIR2 = PIR sensor
  Bauteil1 = Breadboard Power Supply Board SMD
  C1 = Electrolytic Capacitor [capacitance=100µF package="200 mil [THT, electrolytic]"]
  S1 = Pushbutton [package="[THT]"]
  S2 = Pushbutton [package="[THT]"]
  Bauteil2 = FTDI Basic Programmer

nets:
  VDD: MOD-WIFI-ESP8266-DEV1.3.3V, PIR1.VDD, PIR2.VDD, Bauteil1.VCC, C1.+
  GND: MOD-WIFI-ESP8266-DEV1.GND, MOD-WIFI-ESP8266-DEV1.RSTB, MOD-WIFI-ESP8266-DEV1.GPIO16, MOD-WIFI-ESP8266-DEV1.GPIO0, PIR1.GND, PIR2.GND, Bauteil1.GND, C1.-, S1.Pin_1, S1.Pin_2, S1.Pin_3, S1.Pin_4, S2.Pin_1, S2.Pin_2, S2.Pin_3, S2.Pin_4, Bauteil2.GND
  N1: MOD-WIFI-ESP8266-DEV1.GPIO1, Bauteil2.TXO
  N2: MOD-WIFI-ESP8266-DEV1.GPIO3, Bauteil2.RXI
  N3: MOD-WIFI-ESP8266-DEV1.GPIO12, PIR2.SIG
  N4: MOD-WIFI-ESP8266-DEV1.GPIO13, PIR1.SIG

custom parts:
  Olimex ESP8266 DEV: MOD-WIFI-ESP8266-DEV is the ultimate development board for ESP8266 with all GPIOs and resources exposed, can be soldered to PCB or used with breadboard and UEXT. Small U.FL connector is provided for external antenna connection. ESP8266 is very highly integrated SOC which includes Xtensa LX106 core processor, RAM, RF front end and allow WIFI TCP-IP stack to be implemented on board with just few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
